// Logisim project IF.circ as structural Verilog: 1 circuit, main circuit IF
module IF (
  input  [7:0] i1,
  input  [7:0] i2,
  input  s1,
  input  s0,
  input  clk,
  output [7:0] PC_1,
  output [3:0] r3_im,
  output [3:0] r2,
  output [7:0] j,
  output [3:0] r1,
  output [3:0] op
);

  wire [7:0] multiplexer_1_out, register_1_q;

  Multiplexer #(.select(2), .width(8), .enable("false")) multiplexer_1 (
    .in0(PC_1), .in1(i1), .in2(i2), .in3(i2), .out(multiplexer_1_out), .sel({s1, s0}));
  Register register_1 (.D(multiplexer_1_out), .en(1'b1), .Q(register_1_q), .clk(clk), .clr(1'b0));
  Adder adder_1 (.a(8'h1), .b(register_1_q), .out(PC_1), .cin(1'b0));  // open: cout
  ROM #(.dataWidth(16)) rom_1 (.addr(register_1_q), .data({op, j, r3_im}));  // open: sel

  assign r1 = j[7:4];
  assign r2 = j[3:0];

  // Notes on the sheet:
  //   contents of rom_1 (hex, n*v repeats v):
  //   b20a b305 d123 d413 d541 e323 1221 9241 8150 c551 a222 2441 f323 5124 6315 8140 115 733a 4333 8150
  //   313b
endmodule
